# Fritzing sketch M01_Time-On (saved by Fritzing 1.0.4)
breadboards: 3

parts:
  Breadboard4 = Breadboard Split Power
  Breadboard5 = Breadboard Split Power
  Neopixel1 = Adafruit RBG Smart Neopixel [package="DIP (Dual Inline) [THT]"]
  Neopixel2 = Adafruit RBG Smart Neopixel [package="DIP (Dual Inline) [THT]"]
  Neopixel3 = Adafruit RBG Smart Neopixel [package="DIP (Dual Inline) [THT]"]
  Neopixel4 = Adafruit RBG Smart Neopixel [package="DIP (Dual Inline) [THT]"]
  U1 = ENCODER_RGB [package=encoder_led_2]
  A1 = Particle - Photon2
  J1 = Piezo Speaker
  OLED_I2C1 = OLED 128x64 I2C Monochrome Display
  M1 = BMP280
  S1 = Pushbutton [package="[THT]"]
  S2 = Pushbutton [package="[THT]"]
  S5 = Pushbutton [package="[THT]"]
  S4 = Pushbutton [package="[THT]"]
  R1 = Resistor [tolerance=±5% resistance=10k package="1206 [SMD]"]
  R2 = Resistor [tolerance=±5% resistance=10k package="1206 [SMD]"]
  R3 = Resistor [tolerance=±5% resistance=10k package="1206 [SMD]"]
  R4 = Resistor [tolerance=±5% resistance=10k package="1206 [SMD]"]
  S6 = Round Pushbutton
  LED1 = LED - 3mm [color="Red (635nm)" current=0.030A package="3 mm [THT]"]
  LED2 = LED - 3mm [color="Blue (470nm)" current=0.030A package="3 mm [THT]"]
  LED3 = LED - 3mm [color="Yellow (595nm)" current=0.030A package="3 mm [THT]"]
  LED4 = LED - 3mm [color="Green (565nm)" current=0.030A package="3 mm [THT]"]
  R5 = Resistor [tolerance=±5% resistance=220 package="1206 [SMD]"]  # not connected
  R6 = Resistor [tolerance=±5% resistance=220 package="1206 [SMD]"]
  R7 = Resistor [tolerance=±5% resistance=220 package="1206 [SMD]"]
  R8 = Resistor [tolerance=±5% resistance=220 package="1206 [SMD]"]

nets:
  GND: Breadboard4.pin3Z, Breadboard4.pin20Z, Breadboard4.pin29Z, Breadboard5.pin3Z, Breadboard5.pin11Z, Breadboard5.pin28Z, Neopixel1.G, Neopixel3.G, Neopixel4.G, U1.C, A1.Pin_4, A1.Pin_30, A1.Pin_35, J1.pin1, OLED_I2C1.GND, M1.GND, R1.Pin_1, R2.Pin_1, R3.Pin_1, R4.Pin_1, R6.Pin_1, R7.Pin_1, R8.Pin_1
  VDD: Breadboard4.pin4Y, Breadboard4.pin15Y, Breadboard4.pin17Y, Breadboard4.pin21Y, Breadboard4.pin29Y, Breadboard5.pin3Y, Breadboard5.pin15Y, Breadboard5.pin17Y, Breadboard5.pin29Y, U1.+, OLED_I2C1.VDD, M1.VIN, S1.Pin_3, S1.Pin_4, S2.Pin_3, S2.Pin_4, S5.Pin_3, S5.Pin_4, S4.Pin_3, S4.Pin_4, S6.leg1
  N1: Neopixel1.+, Neopixel3.+, Neopixel4.+, A1.Pin_26
  N2: Neopixel1.In, A1.Pin_19
  N3: Neopixel1.O, Neopixel2.In
  N4: Neopixel2.O, Neopixel3.In
  N5: Neopixel3.O, Neopixel4.In
  N6: U1.B#2, A1.Pin_15
  N7: U1.A, A1.Pin_14
  N8: U1.R, A1.Pin_11
  N9: U1.G, A1.Pin_10
  N10: U1.SW, A1.Pin_13
  N11: U1.B#8, A1.Pin_9
  N12: A1.Pin_5, LED1.anode
  N13: A1.Pin_6, LED2.anode
  N14: A1.Pin_7, LED3.anode
  N15: A1.Pin_8, LED4.anode
  N16: A1.Pin_12, J1.pin2
  N17: A1.Pin_17, OLED_I2C1.SDA, M1.SDA
  N18: A1.Pin_18, OLED_I2C1.SCK, M1.SCL
  N19: A1.Pin_20, S6.leg0
  N20: A1.Pin_21, S4.Pin_1, S4.Pin_2, R1.Pin_0
  N21: A1.Pin_22, S5.Pin_1, S5.Pin_2, R2.Pin_0
  N22: A1.Pin_23, A1.Pin_37, S2.Pin_1, S2.Pin_2, R3.Pin_0
  N23: A1.Pin_25, S1.Pin_1, S1.Pin_2, R4.Pin_0
  N24: LED1.cathode, R8.Pin_0
  N25: LED2.cathode, R7.Pin_0
  N26: LED3.cathode, R6.Pin_0

custom parts:
  Breadboard Split Power: A custom 6 pin per group power supply strip where the top row (ground) is all bussed together and the bottom row (+V) is split in two groups of 12 pins. This version is modified to be a loadable part and was rescaled to be on the standard 1px = 1thou grid with the size set in inches
  ENCODER_RGB: SparkFun RGB rotary Encoder
  Particle - Photon2: The Photon 2 is a microcontroller and Wi-Fi networking developed by particle. Features: 802.11a/b/g/n Wi-Fi, 2.4 GHz and 5 GHz Integrated PCB antenna Integrated U.FL connector for external antenna Integrated RF switch BLE 5 using same antenna as Wi-Fi Realtek RTL8721DM MCU ARM Cortex M33 CPU, 200 MHz 2048 KB (2 MB) user application maximum size 3072 KB (3 MB) of RAM available to user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
  BMP280: Temperature Humidity Barometric presure Sensor, I2C
  Pushbutton: A generic pushbutton.
  Pushbutton: A generic pushbutton.
  Pushbutton: A generic pushbutton.
  Pushbutton: A generic pushbutton.
